// Logisim project SequenceReconizer.circ as structural Verilog: 10 circuits, main circuit main
module main (
  input  RESET,
  input  X
);

  wire bitdetector_1_s1, bitdetector_1_s2, bitdetector_1_s3, clock_1_out;
  wire [2:0] encodersbintobcd_1_n1d1_2, encodersbintobcd_1_n1d2_2, encodersbintobcd_1_n1d3_2,
       encodersbintobcd_1_n2d1_2, encodersbintobcd_1_n2d2_2, encodersbintobcd_1_n2d3_2,
       encodersbintobcd_1_n3d1_2, encodersbintobcd_1_n3d2_2, encodersbintobcd_1_n3d3_2;
  wire [3:0] binarytodecimal_1_d, binarytodecimal_1_u, bitdetector_1_currentstate, encodersbintobcd_1_n1d1,
       encodersbintobcd_1_n1d2, encodersbintobcd_1_n1d3, encodersbintobcd_1_n2d1, encodersbintobcd_1_n2d2,
       encodersbintobcd_1_n2d3, encodersbintobcd_1_n3d1, encodersbintobcd_1_n3d2, encodersbintobcd_1_n3d3,
       undriven;
  wire [6:0] view_1_g_f_a_b_e_d_c, view_2_g_f_a_b_e_d_c;
  wire [7:0] counters_1_c1, counters_1_c2, counters_1_c3;

  Clock clock_1 (.out(clock_1_out));
  BitDetector bitdetector_1 (
    .Clock(clock_1_out), .Reset(RESET), .X(X), .S1(bitdetector_1_s1), .S2(bitdetector_1_s2),
    .S3(bitdetector_1_s3), .CurrentState(bitdetector_1_currentstate));
  BinaryToDecimal binarytodecimal_1 (
    .B({undriven, bitdetector_1_currentstate}), .d(binarytodecimal_1_d), .u(binarytodecimal_1_u));  // open: c
  View view_1 (.D(binarytodecimal_1_d), .g_f_a_b_e_d_c(view_1_g_f_a_b_e_d_c));
  View view_2 (.D(binarytodecimal_1_u), .g_f_a_b_e_d_c(view_2_g_f_a_b_e_d_c));
  Counters counters_1 (
    .C1in(bitdetector_1_s1), .C2in(bitdetector_1_s2), .C3in(bitdetector_1_s3), .RESET(RESET),
    .C1(counters_1_c1), .C2(counters_1_c2), .C3(counters_1_c3));
  _7_Segment_Display u_7_segment_display_1 (
    .g(view_1_g_f_a_b_e_d_c[0]), .f(view_1_g_f_a_b_e_d_c[1]), .a(view_1_g_f_a_b_e_d_c[2]),
    .b(view_1_g_f_a_b_e_d_c[3]), .e(view_1_g_f_a_b_e_d_c[4]), .d(view_1_g_f_a_b_e_d_c[5]),
    .c(view_1_g_f_a_b_e_d_c[6]));  // open: dp
  _7_Segment_Display u_7_segment_display_2 (
    .g(view_2_g_f_a_b_e_d_c[0]), .f(view_2_g_f_a_b_e_d_c[1]), .a(view_2_g_f_a_b_e_d_c[2]),
    .b(view_2_g_f_a_b_e_d_c[3]), .e(view_2_g_f_a_b_e_d_c[4]), .d(view_2_g_f_a_b_e_d_c[5]),
    .c(view_2_g_f_a_b_e_d_c[6]));  // open: dp
  EncodersBinToBCD encodersbintobcd_1 (
    .N3(counters_1_c1), .N2(counters_1_c2), .N1(counters_1_c3),
    .N1D1({encodersbintobcd_1_n1d1_2, encodersbintobcd_1_n1d1}),
    .N1D2({encodersbintobcd_1_n1d2_2, encodersbintobcd_1_n1d2}),
    .N1D3({encodersbintobcd_1_n1d3_2, encodersbintobcd_1_n1d3}),
    .N2D1({encodersbintobcd_1_n2d1_2, encodersbintobcd_1_n2d1}),
    .N2D2({encodersbintobcd_1_n2d2_2, encodersbintobcd_1_n2d2}),
    .N2D3({encodersbintobcd_1_n2d3_2, encodersbintobcd_1_n2d3}),
    .N3D1({encodersbintobcd_1_n3d1_2, encodersbintobcd_1_n3d1}),
    .N3D2({encodersbintobcd_1_n3d2_2, encodersbintobcd_1_n3d2}),
    .N3D3({encodersbintobcd_1_n3d3_2, encodersbintobcd_1_n3d3}));
  _7_Segment_Display u_7_segment_display_3 (
    .g(encodersbintobcd_1_n1d1[0]), .f(encodersbintobcd_1_n1d1[1]), .a(encodersbintobcd_1_n1d1[2]),
    .b(encodersbintobcd_1_n1d1[3]), .e(encodersbintobcd_1_n1d1_2[0]), .d(encodersbintobcd_1_n1d1_2[1]),
    .c(encodersbintobcd_1_n1d1_2[2]));  // open: dp
  _7_Segment_Display u_7_segment_display_4 (
    .g(encodersbintobcd_1_n2d1[0]), .f(encodersbintobcd_1_n2d1[1]), .a(encodersbintobcd_1_n2d1[2]),
    .b(encodersbintobcd_1_n2d1[3]), .e(encodersbintobcd_1_n2d1_2[0]), .d(encodersbintobcd_1_n2d1_2[1]),
    .c(encodersbintobcd_1_n2d1_2[2]));  // open: dp
  _7_Segment_Display u_7_segment_display_5 (
    .g(encodersbintobcd_1_n3d1[0]), .f(encodersbintobcd_1_n3d1[1]), .a(encodersbintobcd_1_n3d1[2]),
    .b(encodersbintobcd_1_n3d1[3]), .e(encodersbintobcd_1_n3d1_2[0]), .d(encodersbintobcd_1_n3d1_2[1]),
    .c(encodersbintobcd_1_n3d1_2[2]));  // open: dp
  _7_Segment_Display u_7_segment_display_6 (
    .g(encodersbintobcd_1_n1d2[0]), .f(encodersbintobcd_1_n1d2[1]), .a(encodersbintobcd_1_n1d2[2]),
    .b(encodersbintobcd_1_n1d2[3]), .e(encodersbintobcd_1_n1d2_2[0]), .d(encodersbintobcd_1_n1d2_2[1]),
    .c(encodersbintobcd_1_n1d2_2[2]));  // open: dp
  _7_Segment_Display u_7_segment_display_7 (
    .g(encodersbintobcd_1_n1d3[0]), .f(encodersbintobcd_1_n1d3[1]), .a(encodersbintobcd_1_n1d3[2]),
    .b(encodersbintobcd_1_n1d3[3]), .e(encodersbintobcd_1_n1d3_2[0]), .d(encodersbintobcd_1_n1d3_2[1]),
    .c(encodersbintobcd_1_n1d3_2[2]));  // open: dp
  _7_Segment_Display u_7_segment_display_8 (
    .g(encodersbintobcd_1_n2d2[0]), .f(encodersbintobcd_1_n2d2[1]), .a(encodersbintobcd_1_n2d2[2]),
    .b(encodersbintobcd_1_n2d2[3]), .e(encodersbintobcd_1_n2d2_2[0]), .d(encodersbintobcd_1_n2d2_2[1]),
    .c(encodersbintobcd_1_n2d2_2[2]));  // open: dp
  _7_Segment_Display u_7_segment_display_9 (
    .g(encodersbintobcd_1_n2d3[0]), .f(encodersbintobcd_1_n2d3[1]), .a(encodersbintobcd_1_n2d3[2]),
    .b(encodersbintobcd_1_n2d3[3]), .e(encodersbintobcd_1_n2d3_2[0]), .d(encodersbintobcd_1_n2d3_2[1]),
    .c(encodersbintobcd_1_n2d3_2[2]));  // open: dp
  _7_Segment_Display u_7_segment_display_10 (
    .g(encodersbintobcd_1_n3d2[0]), .f(encodersbintobcd_1_n3d2[1]), .a(encodersbintobcd_1_n3d2[2]),
    .b(encodersbintobcd_1_n3d2[3]), .e(encodersbintobcd_1_n3d2_2[0]), .d(encodersbintobcd_1_n3d2_2[1]),
    .c(encodersbintobcd_1_n3d2_2[2]));  // open: dp
  _7_Segment_Display u_7_segment_display_11 (
    .g(encodersbintobcd_1_n3d3[0]), .f(encodersbintobcd_1_n3d3[1]), .a(encodersbintobcd_1_n3d3[2]),
    .b(encodersbintobcd_1_n3d3[3]), .e(encodersbintobcd_1_n3d3_2[0]), .d(encodersbintobcd_1_n3d3_2[1]),
    .c(encodersbintobcd_1_n3d3_2[2]));  // open: dp

  // Other names for the same wires on the sheet: R = RESET
endmodule

module BitDetector (
  input  Clock,
  input  Reset,
  input  X,
  output S1,
  output S2,
  output S3,
  output [3:0] CurrentState
);

  wire and_2_out, and_3_out, and_4_out, and_5_out, and_6_out, and_7_out, and_8_out, and_9_out, and_10_out,
       and_11_out, and_12_out, and_13_out, and_14_out, and_15_out, and_16_out, and_17_out, and_18_out,
       and_19_out, and_20_out, and_21_out, J0, J1, J2, J3, K0, K1, K2, K3, not_1_out, not_2_out, not_3_out,
       not_4_out, not_5_out;

  not not_1 (not_1_out, CurrentState[3]);
  not not_2 (not_2_out, CurrentState[2]);
  not not_3 (not_3_out, CurrentState[1]);
  not not_4 (not_4_out, CurrentState[0]);
  not not_5 (not_5_out, X);
  and and_1 (J3, CurrentState[2], CurrentState[1], CurrentState[0]);
  or or_1 (K3, X, CurrentState[0], CurrentState[1]);
  and and_2 (and_2_out, not_1_out, CurrentState[1], not_4_out, X);
  and and_3 (and_3_out, CurrentState[1], CurrentState[0], not_5_out);
  and and_4 (and_4_out, CurrentState[3], not_3_out, not_4_out, X);
  and and_5 (and_5_out, CurrentState[3], CurrentState[0], not_5_out);
  and and_6 (and_6_out, not_3_out, not_5_out);
  and and_7 (and_7_out, CurrentState[0], not_5_out);
  and and_8 (and_8_out, CurrentState[1], X);
  and and_9 (and_9_out, not_1_out, not_2_out, CurrentState[0]);
  and and_10 (and_10_out, CurrentState[0], X);
  and and_11 (and_11_out, CurrentState[2], not_4_out);
  and and_12 (and_12_out, CurrentState[3], not_4_out, not_5_out);
  and and_13 (and_13_out, not_2_out, not_4_out);
  and and_14 (and_14_out, CurrentState[2], CurrentState[0]);
  and and_15 (and_15_out, not_1_out, not_2_out, not_3_out, X);
  and and_16 (and_16_out, CurrentState[2], CurrentState[1]);
  and and_17 (and_17_out, CurrentState[3], CurrentState[1], X);
  and and_18 (and_18_out, not_1_out, not_3_out, not_5_out);
  and and_19 (and_19_out, CurrentState[2], not_5_out);
  and and_20 (and_20_out, CurrentState[2], CurrentState[1], not_4_out);
  and and_21 (and_21_out, CurrentState[3], CurrentState[0]);
  and and_22 (S2, CurrentState[3], CurrentState[0]);
  and and_23 (S3, CurrentState[3], CurrentState[1]);
  or or_2 (J2, and_2_out, and_3_out, and_4_out, and_5_out);
  or or_3 (K2, and_6_out, and_7_out, and_8_out);
  or or_4 (J1, and_9_out, and_10_out, and_11_out, and_12_out);
  or or_5 (K1, and_13_out, not_5_out, and_14_out);
  or or_6 (J0, and_15_out, and_16_out, and_17_out);
  or or_7 (K0, and_18_out, and_19_out);
  or or_8 (S1, and_20_out, and_21_out);
  LED led_1 (.in(S1));
  LED led_2 (.in(S2));
  LED led_3 (.in(S3));
  J_K_Flip_Flop j_k_ff_1 (.J(J3), .K(K3), .clk(Clock), .Q(CurrentState[3]), .reset(Reset));  // open: Qn, preset
  J_K_Flip_Flop j_k_ff_2 (.J(J2), .K(K2), .clk(Clock), .Q(CurrentState[2]), .reset(Reset));  // open: Qn, preset
  J_K_Flip_Flop j_k_ff_3 (.J(J1), .K(K1), .clk(Clock), .Q(CurrentState[1]), .reset(Reset));  // open: Qn, preset
  J_K_Flip_Flop j_k_ff_4 (.J(J0), .K(K0), .clk(Clock), .Q(CurrentState[0]), .reset(Reset));  // open: Qn, preset

  // Other names for the same wires on the sheet: Q0 = CurrentState[0]; Q1 = CurrentState[1]; Q2 = CurrentState[2];
  //   Q3 = CurrentState[3]

  // Notes on the sheet:
  //   1011
  //   11011
  //   110100
endmodule

module EventCounter (
  input  Cadd,
  input  RESET,
  output [7:0] Count
);

  wire j_k_ff_1_qn, j_k_ff_2_qn, j_k_ff_3_qn, j_k_ff_4_qn, j_k_ff_5_qn, j_k_ff_6_qn, j_k_ff_7_qn;

  J_K_Flip_Flop j_k_ff_1 (
    .J(1'b1), .K(1'b1), .clk(Cadd), .Q(Count[0]), .Qn(j_k_ff_1_qn), .reset(RESET));  // open: preset
  J_K_Flip_Flop j_k_ff_2 (
    .J(1'b1), .K(1'b1), .clk(j_k_ff_1_qn), .Q(Count[1]), .Qn(j_k_ff_2_qn), .reset(RESET));  // open: preset
  J_K_Flip_Flop j_k_ff_3 (
    .J(1'b1), .K(1'b1), .clk(j_k_ff_2_qn), .Q(Count[2]), .Qn(j_k_ff_3_qn), .reset(RESET));  // open: preset
  J_K_Flip_Flop j_k_ff_4 (
    .J(1'b1), .K(1'b1), .clk(j_k_ff_3_qn), .Q(Count[3]), .Qn(j_k_ff_4_qn), .reset(RESET));  // open: preset
  J_K_Flip_Flop j_k_ff_5 (
    .J(1'b1), .K(1'b1), .clk(j_k_ff_4_qn), .Q(Count[4]), .Qn(j_k_ff_5_qn), .reset(RESET));  // open: preset
  J_K_Flip_Flop j_k_ff_6 (
    .J(1'b1), .K(1'b1), .clk(j_k_ff_5_qn), .Q(Count[5]), .Qn(j_k_ff_6_qn), .reset(RESET));  // open: preset
  J_K_Flip_Flop j_k_ff_7 (
    .J(1'b1), .K(1'b1), .clk(j_k_ff_6_qn), .Q(Count[6]), .Qn(j_k_ff_7_qn), .reset(RESET));  // open: preset
  J_K_Flip_Flop j_k_ff_8 (.J(1'b1), .K(1'b1), .clk(j_k_ff_7_qn), .Q(Count[7]), .reset(RESET));  // open: Qn, preset
endmodule

module BinaryToDecimal (
  input  [7:0] B,
  output [3:0] c,
  output [3:0] d,
  output [3:0] u
);

  wire [7:0] divider_1_out;
  wire [7:4] divider_1_rem, divider_2_out, divider_2_rem;

  Divider divider_1 (.a(B), .b(8'ha), .out(divider_1_out), .rem({divider_1_rem, u}));  // open: upper
  Divider divider_2 (.a(divider_1_out), .b(8'ha), .out({divider_2_out, c}), .rem({divider_2_rem, d}));  // open: upper

  // Notes on the sheet:
  //   Centenas
  //   Decenas
  //   Unidades
endmodule

module View (
  input  [3:0] D,
  output [6:0] g_f_a_b_e_d_c
);

  wire and_1_out, and_2_out, and_3_out, and_4_out, and_5_out, and_6_out, and_7_out, and_8_out, and_9_out,
       and_10_out, and_11_out, and_12_out, and_13_out, and_14_out, and_15_out, and_16_out, not_1_out,
       not_2_out, not_3_out;

  not not_1 (not_1_out, D[2]);
  not not_2 (not_2_out, D[1]);
  not not_3 (not_3_out, D[0]);
  and and_1 (and_1_out, not_1_out, D[1]);
  and and_2 (and_2_out, D[2], not_2_out);
  and and_3 (and_3_out, D[2], not_3_out);
  and and_4 (and_4_out, not_2_out, not_3_out);
  and and_5 (and_5_out, D[2], not_2_out);
  and and_6 (and_6_out, D[2], not_3_out);
  and and_7 (and_7_out, not_1_out, not_3_out);
  and and_8 (and_8_out, D[2], D[0]);
  and and_9 (and_9_out, not_2_out, not_3_out);
  or or_1 (g_f_a_b_e_d_c[3], not_1_out, and_9_out, and_10_out);
  and and_10 (and_10_out, D[1], D[0]);
  and and_11 (and_11_out, not_1_out, not_3_out);
  or or_2 (g_f_a_b_e_d_c[4], and_11_out, and_12_out);
  and and_12 (and_12_out, D[1], not_3_out);
  and and_13 (and_13_out, not_1_out, not_3_out);
  and and_14 (and_14_out, not_1_out, D[1]);
  and and_15 (and_15_out, D[1], not_3_out);
  and and_16 (and_16_out, D[2], not_2_out, D[0]);
  or or_3 (g_f_a_b_e_d_c[6], not_2_out, D[0], D[2]);
  or or_4 (g_f_a_b_e_d_c[0], and_1_out, and_2_out, and_3_out, D[3]);
  or or_5 (g_f_a_b_e_d_c[1], and_4_out, and_5_out, and_6_out, D[3]);
  or or_6 (g_f_a_b_e_d_c[2], and_7_out, D[1], and_8_out, D[3]);
  or or_7 (g_f_a_b_e_d_c[5], and_13_out, and_14_out, and_15_out, and_16_out, D[3]);
endmodule

module Counters (
  input  C1in,
  input  C2in,
  input  C3in,
  input  RESET,
  output [7:0] C1,
  output [7:0] C2,
  output [7:0] C3
);

  EventCounter eventcounter_1 (.Cadd(C1in), .RESET(RESET), .Count(C1));
  EventCounter eventcounter_2 (.Cadd(C2in), .RESET(RESET), .Count(C2));
  EventCounter eventcounter_3 (.Cadd(C3in), .RESET(RESET), .Count(C3));
endmodule

module EncodersBinToBCD (
  input  [7:0] N3,
  input  [7:0] N2,
  input  [7:0] N1,
  output [6:0] N1D1,
  output [6:0] N1D2,
  output [6:0] N1D3,
  output [6:0] N2D1,
  output [6:0] N2D2,
  output [6:0] N2D3,
  output [6:0] N3D1,
  output [6:0] N3D2,
  output [6:0] N3D3
);

  wire [3:0] binarytodecimal_1_c, binarytodecimal_1_d, binarytodecimal_1_u, binarytodecimal_2_c,
       binarytodecimal_2_d, binarytodecimal_2_u, binarytodecimal_3_c, binarytodecimal_3_d,
       binarytodecimal_3_u;

  BinaryToDecimal binarytodecimal_1 (.B(N3), .c(binarytodecimal_1_c), .d(binarytodecimal_1_d), .u(binarytodecimal_1_u));
  BinaryToDecimal binarytodecimal_2 (.B(N2), .c(binarytodecimal_2_c), .d(binarytodecimal_2_d), .u(binarytodecimal_2_u));
  BinaryToDecimal binarytodecimal_3 (.B(N1), .c(binarytodecimal_3_c), .d(binarytodecimal_3_d), .u(binarytodecimal_3_u));
  View view_1 (.D(binarytodecimal_1_c), .g_f_a_b_e_d_c(N1D1));
  View view_2 (.D(binarytodecimal_1_d), .g_f_a_b_e_d_c(N1D2));
  View view_3 (.D(binarytodecimal_1_u), .g_f_a_b_e_d_c(N1D3));
  View view_4 (.D(binarytodecimal_2_c), .g_f_a_b_e_d_c(N2D1));
  View view_5 (.D(binarytodecimal_2_d), .g_f_a_b_e_d_c(N2D2));
  View view_6 (.D(binarytodecimal_2_u), .g_f_a_b_e_d_c(N2D3));
  View view_7 (.D(binarytodecimal_3_c), .g_f_a_b_e_d_c(N3D1));
  View view_8 (.D(binarytodecimal_3_d), .g_f_a_b_e_d_c(N3D2));
  View view_9 (.D(binarytodecimal_3_u), .g_f_a_b_e_d_c(N3D3));
endmodule

module Test1 (
  input  Clk,
  input  Reset,
  output S
);

  wire and_1_out, and_2_out, D0, D1, not_1_out, not_2_out, Q0, Q1;

  not not_1 (not_1_out, Q1);
  not not_2 (not_2_out, Q0);
  and and_1 (and_1_out, not_1_out, Q0);
  and and_2 (and_2_out, Q1, not_2_out);
  or or_1 (D0, not_2_out, Q1);
  or or_2 (S, not_2_out, Q1);
  or or_3 (D1, and_1_out, and_2_out);
  D_Flip_Flop d_ff_1 (.D(D1), .clk(Clk), .Q(Q1), .reset(Reset));  // open: Qn, preset
  D_Flip_Flop d_ff_2 (.D(D0), .clk(Clk), .Q(Q0), .reset(Reset));  // open: Qn, preset
endmodule

module Test2 (
  input  Clk,
  input  Reset,
  output S
);

  wire and_2_out, and_3_out, D0, D1, D2, not_1_out, not_2_out, not_3_out, Q0, Q1, Q2;

  not not_1 (not_1_out, Q2);
  not not_2 (not_2_out, Q1);
  not not_3 (not_3_out, Q0);
  and and_1 (D2, Q1, Q0);
  and and_2 (and_2_out, not_2_out, Q0);
  and and_3 (and_3_out, Q1, not_3_out);
  and and_4 (D0, not_1_out, not_3_out);
  or or_1 (S, not_2_out, Q0);
  or or_2 (D1, and_2_out, and_3_out, Q2);
  D_Flip_Flop d_ff_1 (.D(D2), .clk(Clk), .Q(Q2), .reset(Reset));  // open: Qn, preset
  D_Flip_Flop d_ff_2 (.D(D1), .clk(Clk), .Q(Q1), .reset(Reset));  // open: Qn, preset
  D_Flip_Flop d_ff_3 (.D(D0), .clk(Clk), .Q(Q0), .reset(Reset));  // open: Qn, preset
endmodule

module Test3 (
  input  Clk,
  input  Reset,
  output S
);

  wire and_1_out, and_2_out, and_3_out, and_4_out, and_5_out, and_6_out, D0, D1, D2, not_1_out, not_2_out,
       Q0, Q1, Q2;

  not not_1 (not_1_out, Q2);
  not not_2 (not_2_out, Q1);
  not not_3 (D0, Q0);
  and and_1 (and_1_out, Q1, Q0);
  and and_2 (and_2_out, Q2, D0);
  and and_3 (and_3_out, not_1_out, not_2_out, Q0);
  and and_4 (and_4_out, Q1, D0);
  and and_5 (and_5_out, not_1_out, not_2_out);
  and and_6 (and_6_out, not_1_out, Q0);
  or or_1 (D2, and_1_out, and_2_out);
  or or_2 (D1, and_3_out, and_4_out);
  or or_3 (S, and_5_out, and_6_out);
  D_Flip_Flop d_ff_1 (.D(D2), .clk(Clk), .Q(Q2), .reset(Reset));  // open: Qn, preset
  D_Flip_Flop d_ff_2 (.D(D1), .clk(Clk), .Q(Q1), .reset(Reset));  // open: Qn, preset
  D_Flip_Flop d_ff_3 (.D(D0), .clk(Clk), .Q(Q0), .reset(Reset));  // open: Qn, preset
endmodule
