// Logisim project Lab3Procesador.circ as structural Verilog: 8 circuits, main circuit main
module main (
  input  RESET
);

  wire alu_2_zero, alucontrol_1_jrcontrol, and_2_out, C, clock_1_out, comparator_1_eq, control_1_alusrc,
       control_1_branch, control_1_jump, control_1_memread, control_1_memtoreg, control_1_memwrite,
       control_1_regdst, control_1_regwrite, not_1_out;
  wire [1:0] control_1_aluop;
  wire [3:0] alucontrol_1_aluoperation, fetch_1_pc4_2;
  wire [4:0] ibdown_1_rd, ibdown_1_rs, ibdown_1_rt, ibdown_1_sa, multiplexer_1_out, multiplexer_2_out;
  wire [5:0] ibdown_1_funct, ibdown_1_opcode;
  wire [14:0] ibdown_1_inmediate;
  wire [15:15] ibdown_1_inmediate_2;
  wire [27:0] fetch_1_pc4;
  wire [27:2] ibdown_1_address;
  wire [31:0] alu_1_result, alu_2_result, datamem_1_readdata, fetch_1_pc, I, multiplexer_3_out,
       multiplexer_4_out, multiplexer_5_out, multiplexer_6_out, multiplexer_7_out, multiplexer_8_out,
       regfile_1_readdata1, regfile_1_readdata2;

  Clock clock_1 (.out(clock_1_out));
  and and_1 (C, clock_1_out, not_1_out);
  not not_1 (not_1_out, comparator_1_eq);
  Comparator #(.width(32)) comparator_1 (.a(I), .b({32{1'b0}}), .eq(comparator_1_eq));  // open: gt, lt
  // Probe on multiplexer_6_out
  // Probe on {fetch_1_pc4_2, fetch_1_pc4}
  // Probe on fetch_1_pc
  Fetch fetch_1 (
    .PCnext(multiplexer_6_out), .Clock(C), .Reset(RESET), .PC(fetch_1_pc),
    .PC4({fetch_1_pc4_2, fetch_1_pc4}), .Instruction(I));
  // Probe on I
  IBDown ibdown_1 (
    .Instruction(I), .OPcode(ibdown_1_opcode), .Rs(ibdown_1_rs), .Rt(ibdown_1_rt), .Rd(ibdown_1_rd),
    .SA(ibdown_1_sa), .Funct(ibdown_1_funct), .Inmediate({ibdown_1_inmediate_2[15], ibdown_1_inmediate}),
    .Address(ibdown_1_address));
  Multiplexer #(.width(5)) multiplexer_1 (
    .in0(ibdown_1_rt), .in1(ibdown_1_rd), .out(multiplexer_1_out), .sel(control_1_regdst));
  Multiplexer #(.width(5)) multiplexer_2 (
    .in0(multiplexer_1_out), .in1({5{1'b1}}), .out(multiplexer_2_out), .sel(control_1_jump));
  Control control_1 (
    .OpCode(ibdown_1_opcode), .RegDst(control_1_regdst), .Branch(control_1_branch),
    .MemRead(control_1_memread), .MemWrite(control_1_memwrite), .MemToReg(control_1_memtoreg),
    .ALUSrc(control_1_alusrc), .RegWrite(control_1_regwrite), .Jump(control_1_jump), .ALUOp(control_1_aluop));
  RegFile regfile_1 (
    .ReadReg1(ibdown_1_rs), .ReadReg2(ibdown_1_rt), .WriteReg(multiplexer_2_out),
    .WriteData(multiplexer_8_out), .RegWrite(control_1_regwrite), .Clock(C), .Reset(RESET),
    .ReadData1(regfile_1_readdata1), .ReadData2(regfile_1_readdata2));
  Multiplexer #(.width(32)) multiplexer_3 (
    .in0(regfile_1_readdata2), .in1({{17{ibdown_1_inmediate_2[15]}}, ibdown_1_inmediate}),
    .out(multiplexer_3_out), .sel(control_1_alusrc));
  ALUControl alucontrol_1 (
    .ALUOp(control_1_aluop), .Func(ibdown_1_funct), .ALUOperation(alucontrol_1_aluoperation),
    .JRControl(alucontrol_1_jrcontrol));
  ALU alu_1 (
    .ALUOperation(4'b0000), .Input1({fetch_1_pc4_2, fetch_1_pc4}),
    .Input2({{15{ibdown_1_inmediate_2[15]}}, ibdown_1_inmediate, 2'b00}), .Result(alu_1_result));  // open: SAmount, Zero
  ALU alu_2 (
    .ALUOperation(alucontrol_1_aluoperation), .Input1(regfile_1_readdata1), .Input2(multiplexer_3_out),
    .SAmount(ibdown_1_sa), .Zero(alu_2_zero), .Result(alu_2_result));
  Multiplexer #(.width(32)) multiplexer_4 (
    .in0({fetch_1_pc4_2, fetch_1_pc4}), .in1(alu_1_result), .out(multiplexer_4_out), .sel(and_2_out));
  and and_2 (and_2_out, control_1_branch, alu_2_zero);
  Multiplexer #(.width(32)) multiplexer_5 (
    .in0(multiplexer_4_out), .in1({fetch_1_pc4_2, ibdown_1_address, 2'b00}), .out(multiplexer_5_out),
    .sel(control_1_jump));
  Multiplexer #(.width(32)) multiplexer_6 (
    .in0(multiplexer_5_out), .in1(regfile_1_readdata1), .out(multiplexer_6_out), .sel(alucontrol_1_jrcontrol));
  DataMem datamem_1 (
    .Address(alu_2_result), .WriteData(regfile_1_readdata2), .MemWrite(control_1_memwrite),
    .MemRead(control_1_memread), .Clock(C), .Reset(RESET), .ReadData(datamem_1_readdata));
  Multiplexer #(.width(32)) multiplexer_7 (
    .in0(alu_2_result), .in1(datamem_1_readdata), .out(multiplexer_7_out), .sel(control_1_memtoreg));
  Multiplexer #(.width(32)) multiplexer_8 (
    .in0(multiplexer_7_out), .in1({fetch_1_pc4_2, fetch_1_pc4}), .out(multiplexer_8_out), .sel(control_1_jump));

  // Other names for the same wires on the sheet: R = RESET

  // Notes on the sheet:
  //   Procesador Monociclo - MIPS32
endmodule

module Fetch (
  input  [31:0] PCnext,
  input  Clock,
  input  Reset,
  output [31:0] PC,
  output [31:0] PC4,
  output [31:0] Instruction
);

  Register #(.width(32)) PCreg (.D(PCnext), .en(1'b1), .clk(Clock), .Q(PC), .clr(Reset));
  Adder #(.width(32)) adder_1 (.a(32'h4), .b(PC), .out(PC4));  // open: cin, cout
  ROM #(.addrWidth(24), .dataWidth(32)) IM (.addr(PC[25:2]), .data(Instruction));

  // Notes on the sheet:
  //   Componente de Fetch
  //   Valor inicial de PC: 0x00000000
  //   contents of IM (hex, n*v repeats v):
  //   3c090022 95200
endmodule

module IBDown (
  input  [31:0] Instruction,
  output [5:0] OPcode,
  output [4:0] Rs,
  output [4:0] Rt,
  output [4:0] Rd,
  output [4:0] SA,
  output [5:0] Funct,
  output [15:0] Inmediate,
  output [25:0] Address
);


  assign Address = Instruction[25:0];
  assign Funct = Instruction[5:0];
  assign Inmediate = Instruction[15:0];
  assign OPcode = Instruction[31:26];
  assign Rd = Instruction[15:11];
  assign Rs = Instruction[25:21];
  assign Rt = Instruction[20:16];
  assign SA = Instruction[10:6];

  // Other names for the same wires on the sheet: FN[5:0] = Instruction[5:0]; OP[5:0] = Instruction[31:26]

  // Notes on the sheet:
  //   R: op.rs.rt.rd.sa.funct
  //   I: op.rs.rt.inmediate
  //   J: op.address
  //   Componente de Instruction Break Down
endmodule

module RegFile (
  input  [4:0] ReadReg1,
  input  [4:0] ReadReg2,
  input  [4:0] WriteReg,
  input  [31:0] WriteData,
  input  RegWrite,
  input  Clock,
  input  Reset,
  output [31:0] ReadData1,
  output [31:0] ReadData2
);

  wire WE0, WE1, WE2, WE3, WE4, WE5, WE6, WE7, WE8, WE9, WE10, WE11, WE12, WE13, WE14, WE15, WE16, WE17,
       WE18, WE19, WE20, WE21, WE22, WE23, WE24, WE25, WE26, WE27, WE28, WE29, WE30, WE31;
  wire [31:0] R0, R1, R2, R3, R4, R5, R6, R7, R8, R9, R10, R11, R12, R13, R14, R15, R16, R17, R18, R19, R20,
       R21, R22, R23, R24, R25, R26, R27, R28, R29, R30, R31;

  Decoder #(.select(5)) decoder_1 (
    .out0(WE0), .out1(WE1), .out2(WE2), .out3(WE3), .out4(WE4), .out5(WE5), .out6(WE6), .out7(WE7),
    .out8(WE8), .out9(WE9), .out10(WE10), .out11(WE11), .out12(WE12), .out13(WE13), .out14(WE14),
    .out15(WE15), .out16(WE16), .out17(WE17), .out18(WE18), .out19(WE19), .out20(WE20), .out21(WE21),
    .out22(WE22), .out23(WE23), .out24(WE24), .out25(WE25), .out26(WE26), .out27(WE27), .out28(WE28),
    .out29(WE29), .out30(WE30), .out31(WE31), .sel(WriteReg), .en(RegWrite));
  Register #(.width(32)) zero (.D(WriteData), .en(1'b0), .clk(Clock), .Q(R0), .clr(Reset));
  Register #(.width(32)) at (.D(WriteData), .en(WE1), .clk(Clock), .Q(R1), .clr(Reset));
  Register #(.width(32)) v0 (.D(WriteData), .en(WE2), .clk(Clock), .Q(R2), .clr(Reset));
  Register #(.width(32)) v1 (.D(WriteData), .en(WE3), .clk(Clock), .Q(R3), .clr(Reset));
  Register #(.width(32)) a0 (.D(WriteData), .en(WE4), .clk(Clock), .Q(R4), .clr(Reset));
  Register #(.width(32)) a1 (.D(WriteData), .en(WE5), .clk(Clock), .Q(R5), .clr(Reset));
  Register #(.width(32)) a2 (.D(WriteData), .en(WE6), .clk(Clock), .Q(R6), .clr(Reset));
  Register #(.width(32)) a3 (.D(WriteData), .en(WE7), .clk(Clock), .Q(R7), .clr(Reset));
  Register #(.width(32)) t0 (.D(WriteData), .en(WE8), .clk(Clock), .Q(R8), .clr(Reset));
  Register #(.width(32)) t1 (.D(WriteData), .en(WE9), .clk(Clock), .Q(R9), .clr(Reset));
  Register #(.width(32)) t2 (.D(WriteData), .en(WE10), .clk(Clock), .Q(R10), .clr(Reset));
  Register #(.width(32)) t3 (.D(WriteData), .en(WE11), .clk(Clock), .Q(R11), .clr(Reset));
  Register #(.width(32)) t4 (.D(WriteData), .en(WE12), .clk(Clock), .Q(R12), .clr(Reset));
  Register #(.width(32)) t5 (.D(WriteData), .en(WE13), .clk(Clock), .Q(R13), .clr(Reset));
  Register #(.width(32)) t6 (.D(WriteData), .en(WE14), .clk(Clock), .Q(R14), .clr(Reset));
  Register #(.width(32)) t7 (.D(WriteData), .en(WE15), .clk(Clock), .Q(R15), .clr(Reset));
  Register #(.width(32)) s0 (.D(WriteData), .en(WE16), .clk(Clock), .Q(R16), .clr(Reset));
  Register #(.width(32)) s1 (.D(WriteData), .en(WE17), .clk(Clock), .Q(R17), .clr(Reset));
  Register #(.width(32)) s2 (.D(WriteData), .en(WE18), .clk(Clock), .Q(R18), .clr(Reset));
  Register #(.width(32)) s3 (.D(WriteData), .en(WE19), .clk(Clock), .Q(R19), .clr(Reset));
  Register #(.width(32)) s4 (.D(WriteData), .en(WE20), .clk(Clock), .Q(R20), .clr(Reset));
  Register #(.width(32)) s5 (.D(WriteData), .en(WE21), .clk(Clock), .Q(R21), .clr(Reset));
  Register #(.width(32)) s6 (.D(WriteData), .en(WE22), .clk(Clock), .Q(R22), .clr(Reset));
  Register #(.width(32)) s7 (.D(WriteData), .en(WE23), .clk(Clock), .Q(R23), .clr(Reset));
  Register #(.width(32)) t8 (.D(WriteData), .en(WE24), .clk(Clock), .Q(R24), .clr(Reset));
  Register #(.width(32)) t9 (.D(WriteData), .en(WE25), .clk(Clock), .Q(R25), .clr(Reset));
  Register #(.width(32)) k0 (.D(WriteData), .en(WE26), .clk(Clock), .Q(R26), .clr(Reset));
  Register #(.width(32)) k1 (.D(WriteData), .en(WE27), .clk(Clock), .Q(R27), .clr(Reset));
  Register #(.width(32)) gp (.D(WriteData), .en(WE28), .clk(Clock), .Q(R28), .clr(Reset));
  Register #(.width(32)) sp (.D(WriteData), .en(WE29), .clk(Clock), .Q(R29), .clr(Reset));
  Register #(.width(32)) fp (.D(WriteData), .en(WE30), .clk(Clock), .Q(R30), .clr(Reset));
  Register #(.width(32)) ra (.D(WriteData), .en(WE31), .clk(Clock), .Q(R31), .clr(Reset));
  Multiplexer #(.select(5), .width(32)) multiplexer_1 (
    .in0(R0), .in1(R1), .in2(R2), .in3(R3), .in4(R4), .in5(R5), .in6(R6), .in7(R7), .in8(R8), .in9(R9),
    .in10(R10), .in11(R11), .in12(R12), .in13(R13), .in14(R14), .in15(R15), .in16(R16), .in17(R17),
    .in18(R18), .in19(R19), .in20(R20), .in21(R21), .in22(R22), .in23(R23), .in24(R24), .in25(R25),
    .in26(R26), .in27(R27), .in28(R28), .in29(R29), .in30(R30), .in31(R31), .out(ReadData1), .sel(ReadReg1));
  Multiplexer #(.select(5), .width(32)) multiplexer_2 (
    .in0(R0), .in1(R1), .in2(R2), .in3(R3), .in4(R4), .in5(R5), .in6(R6), .in7(R7), .in8(R8), .in9(R9),
    .in10(R10), .in11(R11), .in12(R12), .in13(R13), .in14(R14), .in15(R15), .in16(R16), .in17(R17),
    .in18(R18), .in19(R19), .in20(R20), .in21(R21), .in22(R22), .in23(R23), .in24(R24), .in25(R25),
    .in26(R26), .in27(R27), .in28(R28), .in29(R29), .in30(R30), .in31(R31), .out(ReadData2), .sel(ReadReg2));

  // Other names for the same wires on the sheet: C = Clock; D[31:0] = WriteData; R = Reset; RR1[4:0] = ReadReg1;
  //   RR2[4:0] = ReadReg2; RW = RegWrite; WR[4:0] = WriteReg

  // Notes on the sheet:
  //   Componente de Register File
endmodule

module ALU (
  input  [3:0] ALUOperation,
  input  [31:0] Input1,
  input  [31:0] Input2,
  input  [4:0] SAmount,
  output Zero,
  output [31:0] Result
);

  wire [0:0] comparator_1_lt;
  wire [31:0] adder_1_out, and_1_out, nor_1_out, or_1_out, shifter_1_out, subtractor_1_out;

  Adder #(.width(32)) adder_1 (.a(Input1), .b(Input2), .out(adder_1_out));  // open: cin, cout
  Subtractor #(.width(32)) subtractor_1 (.a(Input1), .b(Input2), .out(subtractor_1_out));  // open: bin, bout
  assign and_1_out = Input1 & Input2;  // AND_Gate and_1, 32 bits wide
  assign or_1_out = Input1 | Input2;  // OR_Gate or_1, 32 bits wide
  assign nor_1_out = ~(Input1 | Input2);  // NOR_Gate nor_1, 32 bits wide
  Comparator #(.width(32)) comparator_1 (.a(Input1), .b(Input2), .lt(comparator_1_lt[0]));  // open: gt, eq
  Shifter #(.width(32)) shifter_1 (.in(Input2), .\dist (SAmount), .out(shifter_1_out));
  Multiplexer #(.select(4), .width(32)) multiplexer_1 (
    .in0(adder_1_out), .in1(subtractor_1_out), .in2(and_1_out), .in3(or_1_out), .in4(nor_1_out),
    .in5({{31{1'b0}}, comparator_1_lt[0]}), .in6(shifter_1_out), .in7({Input2[15:0], {16{1'b0}}}),
    .out(Result), .sel(ALUOperation));  // open: in8, in9, in10, in11, in12, in13, in14, in15
  Comparator #(.width(32)) comparator_2 (.a({32{1'b0}}), .b(Result), .eq(Zero));  // open: gt, lt

  // Other names for the same wires on the sheet: I1[31:0] = Input1; I2[31:0] = Input2; Op[3:0] = ALUOperation;
  //   SA[4:0] = SAmount

  // Notes on the sheet:
  //   Componente unidad Aritmético Lógica (ALU)
  //   ADD, SUB, AND, OR, NOT, SLT, SLL, LUI (SLL16)
endmodule

module DataMem (
  input  [31:0] Address,
  input  [31:0] WriteData,
  input  MemWrite,
  input  MemRead,
  input  Clock,
  input  Reset,
  output [31:0] ReadData
);

  RAM #(.addrWidth(24), .asyncread("true"), .clearpin("true"), .dataWidth(32)) Memory (
    .addr(Address[25:2]), .we(MemWrite), .oe(MemRead), .clk(Clock), .din(WriteData), .dout(ReadData),
    .clr(Reset));

  // Other names for the same wires on the sheet: R = Reset

  // Notes on the sheet:
  //   Componente de Ruta de Datos
endmodule

module Control (
  input  [5:0] OpCode,
  output RegDst,
  output Branch,
  output MemRead,
  output MemWrite,
  output MemToReg,
  output ALUSrc,
  output RegWrite,
  output Jump,
  output [1:0] ALUOp
);

  wire and_1_out, and_2_out, and_4_out, and_5_out, and_7_out, and_8_out, and_9_out, and_10_out, and_11_out,
       and_12_out, and_13_out, not_1_out, not_2_out, not_3_out, not_4_out, not_5_out, not_6_out, not_7_out,
       not_8_out, not_9_out, not_10_out, not_11_out, not_12_out, not_13_out, not_14_out, not_15_out,
       not_16_out;

  not not_1 (not_1_out, OpCode[5]);
  not not_2 (not_2_out, OpCode[3]);
  not not_3 (not_3_out, OpCode[2]);
  not not_4 (not_4_out, OpCode[3]);
  not not_5 (not_5_out, OpCode[5]);
  not not_6 (not_6_out, OpCode[3]);
  not not_7 (not_7_out, OpCode[2]);
  not not_8 (not_8_out, OpCode[1]);
  not not_9 (not_9_out, OpCode[2]);
  not not_10 (not_10_out, OpCode[3]);
  not not_11 (not_11_out, OpCode[3]);
  not not_12 (not_12_out, OpCode[5]);
  not not_13 (not_13_out, OpCode[0]);
  not not_14 (not_14_out, OpCode[5]);
  not not_15 (not_15_out, OpCode[1]);
  not not_16 (not_16_out, OpCode[2]);
  and and_1 (and_1_out, not_1_out, not_2_out);
  and and_2 (and_2_out, OpCode[3], not_3_out);
  and and_3 (Branch, not_4_out, OpCode[2]);
  and and_4 (and_4_out, OpCode[5], not_6_out);
  and and_5 (and_5_out, not_5_out, OpCode[3]);
  and and_6 (MemWrite, OpCode[3], not_7_out);
  and and_7 (and_7_out, not_8_out, not_9_out);
  and and_8 (and_8_out, not_10_out, OpCode[0]);
  and and_9 (and_9_out, OpCode[2], OpCode[0]);
  and and_10 (and_10_out, not_11_out, not_12_out, OpCode[1]);
  and and_11 (and_11_out, not_13_out, OpCode[1]);
  and and_12 (and_12_out, not_14_out, OpCode[0]);
  and and_13 (and_13_out, not_15_out, not_16_out);
  or or_1 (RegDst, and_1_out, and_2_out);
  or or_2 (MemRead, and_4_out, and_5_out);
  or or_3 (Jump, and_10_out, and_11_out);
  or or_4 (ALUOp[0], and_12_out, and_13_out);
  or or_5 (RegWrite, and_7_out, and_8_out, and_9_out);

  assign ALUOp[1] = OpCode[2];
  assign ALUSrc = OpCode[0];
  assign MemToReg = OpCode[5];

  // Other names for the same wires on the sheet: Op2 = OpCode[2]; Op0 = OpCode[0]; Op1 = OpCode[1]; Op3 = OpCode[3];
  //   Op4 = OpCode[4]; Op5 = OpCode[5]

  // Notes on the sheet:
  //   Componente de Control
endmodule

module ALUControl (
  input  [1:0] ALUOp,
  input  [5:0] Func,
  output [3:0] ALUOperation,
  output JRControl
);

  wire and_1_out, and_2_out, and_3_out, and_4_out, and_5_out, and_6_out, and_7_out, and_8_out, and_9_out,
       not_1_out, not_2_out, not_3_out, not_4_out, not_5_out, not_6_out;

  not not_1 (not_1_out, ALUOp[1]);
  not not_2 (not_2_out, Func[5]);
  not not_3 (not_3_out, Func[3]);
  not not_4 (not_4_out, Func[2]);
  not not_5 (not_5_out, Func[1]);
  not not_6 (not_6_out, Func[0]);
  and and_1 (and_1_out, ALUOp[0], not_2_out, not_3_out);
  and and_2 (and_2_out, ALUOp[0], Func[2], Func[1]);
  and and_3 (and_3_out, ALUOp[0], Func[5], Func[3]);
  and and_4 (and_4_out, ALUOp[1], ALUOp[0]);
  and and_5 (and_5_out, ALUOp[0], not_2_out, not_3_out);
  and and_6 (and_6_out, ALUOp[0], Func[2], not_5_out);
  and and_7 (and_7_out, ALUOp[1], ALUOp[0]);
  and and_8 (and_8_out, ALUOp[0], not_5_out, Func[0]);
  and and_9 (and_9_out, ALUOp[0], not_4_out, Func[1]);
  and and_10 (JRControl, not_1_out, ALUOp[0], not_2_out, Func[3], not_4_out, not_5_out, not_6_out);
  or or_1 (ALUOperation[2], and_1_out, and_2_out, and_3_out, and_4_out);
  or or_2 (ALUOperation[1], and_5_out, and_6_out, and_7_out);
  or or_3 (ALUOperation[0], and_8_out, and_9_out, ALUOp[1]);

  assign ALUOperation[3] = 1'b0;

  // Notes on the sheet:
  //   Componente Control de la ALU
endmodule
